# Fritzing sketch quizboard_2_0 (saved by Fritzing 0.9.3b)
circuit board: 1.39778cm x 2.3706cm
circuit board: 1.39778cm x 2.3706cm
circuit board: 8.46667cm x 5.64444cm
breadboards: 5

parts:
  Bauteil1 = Arduino Uno (Rev3)
  R1 = Resistor [tolerance=±5% resistance=220 package=THT]
  R2 = Resistor [tolerance=±5% resistance=220 package=THT]
  R3 = Resistor [tolerance=±5% resistance=220 package=THT]
  R4 = Resistor [tolerance=±5% resistance=220 package=THT]
  R5 = Resistor [tolerance=±5% resistance=220 package=THT]
  R6 = Resistor [tolerance=±5% resistance=220 package=THT]
  R7 = Resistor [tolerance=±5% resistance=220 package=THT]
  R8 = Resistor [tolerance=±5% resistance=220 package=THT]
  LED1 = LED - 5mm [color="Green (565nm)" package="5 mm [THT]"]
  Kont_B = rounded female pin header, 4 pins [form="♀ (female rounded)"]
  Kont_C = rounded female pin header, 4 pins [form="♀ (female rounded)"]
  R37 = Resistor [tolerance=±5% resistance=10M package=THT]
  Kont_A = rounded female pin header, 4 pins [form="♀ (female rounded)"]
  R38 = Resistor [tolerance=±5% resistance=10M package=THT]
  Kont_D = rounded female pin header, 4 pins [form="♀ (female rounded)"]
  R39 = Resistor [tolerance=±5% resistance=10M package=THT]
  R40 = Resistor [tolerance=±5% resistance=10M package=THT]
  Sensor_Buchse = female pin header, 4 pins [form="♀ (female)"]
  R20 = Resistor [tolerance=±5% resistance=1M package=THT]
  R19 = Resistor [tolerance=±5% resistance=1M package=THT]
  R18 = Resistor [tolerance=±5% resistance=1M package=THT]
  R17 = Resistor [tolerance=±5% resistance=1M package=THT]
  R32 = Resistor [tolerance=±5% resistance=1M package=THT]
  R36 = Resistor [tolerance=±5% resistance=1M package=THT]
  R34 = Resistor [tolerance=±5% resistance=1M package=THT]
  R35 = Resistor [tolerance=±5% resistance=1M package=THT]
  R31 = Resistor [tolerance=±5% resistance=1M package=THT]
  R30 = Resistor [tolerance=±5% resistance=1M package=THT]
  R33 = Resistor [tolerance=±5% resistance=1M package=THT]
  R25 = Resistor [tolerance=±5% resistance=1M package=THT]
  LED_Shift = 74HC595 [package="DIP16 [THT]"]
  LED_Bus_Plug = male pin header, 5 pins [form="♂ (male)"]
  LED_Bus_Socket = rounded female pin header, 5 pins [form="♀ (female rounded)"]
  LED2 = LED - 5mm [color="Green (565nm)" package="5 mm [THT]"]
  LED3 = LED - 5mm [color="Green (565nm)" package="5 mm [THT]"]
  LED4 = LED - 5mm [color="Green (565nm)" package="5 mm [THT]"]
  LED5 = LED - 5mm [color="Green (565nm)" package="5 mm [THT]"]
  LED6 = LED - 5mm [color="Green (565nm)" package="5 mm [THT]"]
  LED7 = LED - 5mm [color="Green (565nm)" package="5 mm [THT]"]
  LED8 = LED - 5mm [color="Green (565nm)" package="5 mm [THT]"]
  Plug_Shift = 74HC595 [package="DIP16 [THT]"]
  7_Segment2 = 7 Segment Display
  7Seg_Shift = 74HC595 [package="DIP16 [THT]"]
  R41 = Resistor [tolerance=±5% resistance=220 package=THT]
  R42 = Resistor [tolerance=±5% resistance=220 package=THT]
  R43 = Resistor [tolerance=±5% resistance=220 package=THT]
  R44 = Resistor [tolerance=±5% resistance=220 package=THT]
  R45 = Resistor [tolerance=±5% resistance=220 package=THT]
  R46 = Resistor [tolerance=±5% resistance=220 package=THT]
  R47 = Resistor [tolerance=±5% resistance=220 package=THT]
  R48 = Resistor [tolerance=±5% resistance=220 package=THT]
  Select_Button = Pushbutton [package=THT]
  result_button = Pushbutton [package=THT]
  D1 = Rectifier Diode [part_number=1N4001 package="300 mil [THT]"]
  D2 = Rectifier Diode [part_number=1N4001 package="300 mil [THT]"]
  D3 = Rectifier Diode [part_number=1N4001 package="300 mil [THT]"]
  D4 = Rectifier Diode [part_number=1N4001 package="300 mil [THT]"]
  D5 = Rectifier Diode [part_number=1N4001 package="300 mil [THT]"]
  D6 = Rectifier Diode [part_number=1N4001 package="300 mil [THT]"]
  D7 = Rectifier Diode [part_number=1N4001 package="300 mil [THT]"]
  D8 = Rectifier Diode [part_number=1N4001 package="300 mil [THT]"]
  J2 = male pin header, 2 pins [form="♂ (male)"]
  J3 = male pin header, 2 pins [form="♂ (male)"]
  J4 = male pin header, 2 pins [form="♂ (male)"]
  J5 = male pin header, 2 pins [form="♂ (male)"]
  J6 = male pin header, 2 pins [form="♂ (male)"]
  J7 = male pin header, 2 pins [form="♂ (male)"]
  J9 = male pin header, 2 pins [form="♂ (male)"]
  J10 = male pin header, 2 pins [form="♂ (male)"]
  J11 = male pin header, 2 pins [form="♂ (male)"]
  J12 = male pin header, 2 pins [form="♂ (male)"]
  J13 = male pin header, 2 pins [form="♂ (male)"]
  J14 = male pin header, 2 pins [form="♂ (male)"]
  J15 = male pin header, 2 pins [form="♂ (male)"]
  J1 = male pin header, 2 pins [form="♂ (male)"]
  J8 = male pin header, 3 pins [form="♂ (male)"]
  J16 = male pin header, 3 pins [form="♂ (male)"]

nets:
  N1: Bauteil1.A0, R37.Pin_1, Kont_A.pin1, Sensor_Buchse.pin4, R17.Pin_0, R33.Pin_1
  N2: Bauteil1.A1, Kont_B.pin1, R38.Pin_1, Sensor_Buchse.pin3, R18.Pin_0, R30.Pin_1
  N3: Bauteil1.A2, Kont_C.pin1, R39.Pin_1, Sensor_Buchse.pin2, R19.Pin_0, R31.Pin_1
  N4: Bauteil1.A3, Kont_D.pin1, R40.Pin_1, Sensor_Buchse.pin1, R20.Pin_0, R32.Pin_1
  N5: Bauteil1.D8, Plug_Shift.ST_CP
  N6: Bauteil1.D9_PWM, Plug_Shift.SH_CP
  N7: Bauteil1.D10_PWM/SS, LED_Bus_Plug.pin5, LED_Bus_Socket.pin5, 7Seg_Shift.DS
  N8: Bauteil1.D11_PWM/MOSI, LED_Shift.ST_CP, LED_Bus_Plug.pin3, LED_Bus_Socket.pin3, 7Seg_Shift.ST_CP
  N9: Bauteil1.D12/MISO, LED_Shift.SH_CP, LED_Bus_Plug.pin2, LED_Bus_Socket.pin2, 7Seg_Shift.SH_CP
  N10: Bauteil1.D2, result_button.leg1
  N11: Bauteil1.D3_PWM, Select_Button.leg1
  N12: Bauteil1.D7, Plug_Shift.DS
  VCC: Bauteil1.5V, LED_Shift.MR, LED_Shift.VCC, LED_Bus_Plug.pin1, LED_Bus_Socket.pin1, Plug_Shift.MR, Plug_Shift.VCC, 7_Segment2.common_anode, 7Seg_Shift.MR, 7Seg_Shift.VCC
  GND: Bauteil1.GND, LED1.anode, R20.Pin_1, R19.Pin_1, R18.Pin_1, R17.Pin_1, LED_Shift.GND, LED_Shift.OE, LED_Bus_Plug.pin4, LED_Bus_Socket.pin4, LED2.anode, LED3.anode, LED4.anode, LED5.anode, LED6.anode, LED7.anode, LED8.anode, Plug_Shift.GND, Plug_Shift.OE, 7Seg_Shift.GND, 7Seg_Shift.OE, Select_Button.leg0, result_button.leg0, J8.pin3, J16.pin1
  N13: R1.Pin_0, LED_Shift.Q7
  N14: R1.Pin_1, LED1.cathode, J8.pin1, J16.pin3
  N15: R2.Pin_0, LED_Shift.Q6
  N16: R2.Pin_1, LED2.cathode, J7.pin1, J15.pin2
  N17: R3.Pin_0, LED_Shift.Q5
  N18: R3.Pin_1, LED3.cathode, J6.pin1, J14.pin2
  N19: R4.Pin_0, LED_Shift.Q4
  N20: R4.Pin_1, LED4.cathode, J5.pin1, J13.pin2
  N21: R5.Pin_0, LED_Shift.Q3
  N22: R5.Pin_1, LED5.cathode, J4.pin1, J12.pin2
  N23: R6.Pin_0, LED_Shift.Q2
  N24: R6.Pin_1, LED6.cathode, J3.pin1, J11.pin2
  N25: R7.Pin_0, LED_Shift.Q0
  N26: R7.Pin_1, LED8.cathode, J9.pin2, J1.pin1
  N27: R8.Pin_0, LED_Shift.Q1
  N28: R8.Pin_1, LED7.cathode, J2.pin1, J10.pin2
  N29: Kont_B.pin2, R34.Pin_0, R30.Pin_0
  N30: Kont_B.pin3, R34.Pin_1
  N31: Kont_B.pin4, R38.Pin_0
  N32: Kont_C.pin2, R35.Pin_0, R31.Pin_0
  N33: Kont_C.pin3, R35.Pin_1
  N34: Kont_C.pin4, R39.Pin_0
  N35: R37.Pin_0, Kont_A.pin4
  N36: Kont_A.pin2, R33.Pin_0, R25.Pin_0
  N37: Kont_A.pin3, R25.Pin_1
  N38: Kont_D.pin2, R32.Pin_0, R36.Pin_0
  N39: Kont_D.pin3, R36.Pin_1
  N40: Kont_D.pin4, R40.Pin_0
  N41: LED_Shift.DS, 7Seg_Shift.Q7'
  N42: Plug_Shift.Q1, D2.anode
  N43: Plug_Shift.Q2, D3.anode
  N44: Plug_Shift.Q3, D4.anode
  N45: Plug_Shift.Q4, D5.anode
  N46: Plug_Shift.Q5, D6.anode
  N47: Plug_Shift.Q6, D7.anode
  N48: Plug_Shift.Q7, D8.anode
  N49: Plug_Shift.Q0, D1.anode
  N50: 7_Segment2.Segment_E, R45.Pin_1
  N51: 7_Segment2.Segment_D, R46.Pin_1
  N52: 7_Segment2.Segment_C, R48.Pin_1
  N53: 7_Segment2.Segment_DP, R47.Pin_1
  N54: 7_Segment2.Segment_B, R44.Pin_1
  N55: 7_Segment2.Segment_A, R43.Pin_1
  N56: 7_Segment2.Segment_F, R41.Pin_1
  N57: 7_Segment2.Segment_G, R42.Pin_0
  N58: 7Seg_Shift.Q1, R44.Pin_0
  N59: 7Seg_Shift.Q2, R43.Pin_0
  N60: 7Seg_Shift.Q3, R41.Pin_0
  N61: 7Seg_Shift.Q4, R47.Pin_0
  N62: 7Seg_Shift.Q5, R46.Pin_0
  N63: 7Seg_Shift.Q6, R45.Pin_0
  N64: 7Seg_Shift.Q7, R48.Pin_0
  N65: 7Seg_Shift.Q0, R42.Pin_1
  N66: D1.cathode, J9.pin1, J1.pin2
  N67: D2.cathode, J2.pin2, J10.pin1
  N68: D3.cathode, J3.pin2, J11.pin1
  N69: D4.cathode, J4.pin2, J12.pin1
  N70: D5.cathode, J5.pin2, J13.pin1
  N71: D6.cathode, J6.pin2, J14.pin1
  N72: D7.cathode, J7.pin2, J15.pin1
  N73: D8.cathode, J8.pin2, J16.pin2
